// Logisim project Basic_Logic_Blocks.circ as structural Verilog: 1 circuit, main circuit main
module main (
  input  AND_Gates,
  input  in_2,
  input  in_3,
  input  in_4,
  input  in_5,
  input  in_6,
  input  in_7,
  input  in_8,
  input  in_9,
  input  in_10,
  input  in_11,
  input  in_12,
  input  a,
  input  a_2,
  input  a_b,
  input  a_b_2,
  input  b,
  input  b_2,
  input  in_19,
  input  in_20,
  input  a_3,
  input  a_prime
);

  wire and_1_out, and_2_out, and_3_out, not_1_out, not_2_out, or_1_out, or_2_out, or_3_out;

  and and_1 (and_1_out, AND_Gates, in_5);
  and and_2 (and_2_out, in_7, in_11);
  and and_3 (and_3_out, a, b);
  not not_1 (not_1_out, in_19);
  not not_2 (not_2_out, a_3);
  or or_1 (or_1_out, in_2, in_6);
  or or_2 (or_2_out, in_8, in_12);
  or or_3 (or_3_out, a_2, b_2);

  // Notes on the sheet:
  //   NOT Gate
  //   OR Gates
endmodule
